// Logisim project Controller.circ as structural Verilog: 1 circuit, main circuit Controller
module Controller (
  input  [15:0] Inst,
  input  [3:0] FlagsIn,
  input  Clk,
  input  Reset,
  input  [31:0] R0,
  input  [31:0] R1,
  input  [31:0] R2,
  input  [31:0] R3,
  input  [31:0] R4,
  input  [31:0] R5,
  input  [31:0] R6,
  input  [31:0] R7,
  input  [31:0] RAM_Value,
  output Carry,
  output DP_Shift,
  output Imm32_Enable,
  output [4:0] Imm5,
  output [31:0] Imm32,
  output [3:0] ALU_Opcode,
  output [2:0] Rm,
  output [2:0] Rn,
  output [2:0] Rd,
  output [3:0] Flags,
  output [31:0] RAM_Addr,
  output Load,
  output Store,
  output PC_Hold,
  output [2:0] Mask,
  output [31:0] SP,
  output [31:0] PC
);

  wire and_2_out, and_3_out, and_4_out, and_5_out, and_6_out, and_7_out, and_8_out, and_10_out,
       comparator_1_eq, comparator_2_eq, comparator_3_eq, comparator_4_eq, comparator_5_eq, comparator_6_eq,
       comparator_7_eq, conditional_1_verified, load_address_1_imm32_enable, not_1_out, not_2_out,
       opcode_decoder_1_conditional, opcode_decoder_1_data_processing, opcode_decoder_1_high_register_op,
       opcode_decoder_1_load_address, opcode_decoder_1_load_store, opcode_decoder_1_long_branch,
       opcode_decoder_1_shift, opcode_decoder_1_signextend, opcode_decoder_1_sp_address, or_2_out, or_5_out,
       or_6_out, or_7_out, or_8_out, or_9_out, or_11_out, or_13_out, shift_add_sub_mov_1_carry,
       shift_add_sub_mov_1_imm32_enable, sp_address_1_write_enable;
  wire [2:0] controlled_buffer_2_out, data_processing_1_rd, data_processing_1_rm, data_processing_1_rn,
       load_address_1_rd, load_store_1_rmd, or_3_out, pull_resistor_2_node, pull_resistor_4_node,
       shift_add_sub_mov_1_rd, shift_add_sub_mov_1_rm, shift_add_sub_mov_1_rn;
  wire [3:0] controlled_buffer_6_out, controlled_buffer_9_out, data_processing_1_alu_opcode,
       data_processing_1_flags_update_mask, load_address_1_alu_opcode, or_1_out, or_10_out,
       pull_resistor_5_node, shift_add_sub_mov_1_alu_opcode, shift_add_sub_mov_1_flags_update_mask;
  wire [7:0] multiplexer_2_out;
  wire [10:0] conditional_1_offset, or_4_out, pull_resistor_1_node;
  wire [31:0] adder_1_out, adder_2_out, adder_3_out, adder_4_out, adder_5_out, adder_6_out, adder_7_out,
       and_1_out, and_9_out, bit_extender_1_out, bit_extender_2_out, bit_extender_3_out, bit_extender_4_out,
       bit_extender_5_out, controlled_buffer_12_out, load_address_1_imm32, load_store_1_imm32, LR_Value,
       multiplexer_1_out, multiplexer_3_out, multiplexer_4_out, multiplexer_5_out, multiplexer_7_out,
       multiplier_1_out, negator_1_out, negator_2_out, or_12_out, or_14_out, or_22_out, pull_resistor_6_node,
       pull_resistor_7_node, pull_resistor_10_node, pull_resistor_11_node, pull_resistor_12_node,
       pull_resistor_13_node, shift_add_sub_mov_1_imm32, sp_address_1_new_stack_pointer, subtractor_1_out;
  wire [31:8] multiplexer_2_out_2;

  Register #(.width(32)) Stack_Pointer (
    .D(sp_address_1_new_stack_pointer), .en(sp_address_1_write_enable), .clk(Clk), .Q(SP), .clr(Reset));
  Opcode_Decoder opcode_decoder_1 (
    .Opcode(Inst[15:9]), .Shift(opcode_decoder_1_shift), .Load_Store(opcode_decoder_1_load_store),
    .SP_Address(opcode_decoder_1_sp_address), .Conditional(opcode_decoder_1_conditional),
    .Load_Address(opcode_decoder_1_load_address), .Long_Branch(opcode_decoder_1_long_branch),
    .High_Register_Op(opcode_decoder_1_high_register_op), .Data_Processing(opcode_decoder_1_data_processing),
    .SignExtend(opcode_decoder_1_signextend));
  Adder #(.width(32)) adder_1 (.a(PC), .b(32'h4), .out(adder_1_out));  // open: cin, cout
  assign and_1_out = adder_1_out & ~32'h2;  // AND_Gate and_1, 32 bits wide
  assign or_1_out = data_processing_1_flags_update_mask | shift_add_sub_mov_1_flags_update_mask;  // OR_Gate or_1, 4 bits wide
  Comparator #(.width(4)) comparator_1 (.a(Inst[9:6]), .b(4'b1101), .eq(comparator_1_eq));  // open: gt, lt
  Comparator #(.width(4)) comparator_2 (.a(Inst[9:6]), .b(4'b1000), .eq(comparator_2_eq));  // open: gt, lt
  Comparator #(.width(4)) comparator_3 (.a(Inst[9:6]), .b(4'b1001), .eq(comparator_3_eq));  // open: gt, lt
  Comparator #(.width(4)) comparator_4 (.a(Inst[9:6]), .b(4'b0001), .eq(comparator_4_eq));  // open: gt, lt
  Comparator #(.width(4)) comparator_5 (.a(Inst[9:6]), .b(4'b1010), .eq(comparator_5_eq));  // open: gt, lt
  Comparator #(.width(4)) comparator_6 (.a(Inst[9:6]), .b(4'b0010), .eq(comparator_6_eq));  // open: gt, lt
  Comparator #(.width(4)) comparator_7 (.a(Inst[9:6]), .b(4'b1110), .eq(comparator_7_eq));  // open: gt, lt
  Pull_Resistor pull_resistor_1 (.node(pull_resistor_1_node));
  assign pull_resistor_1_node = opcode_decoder_1_long_branch ? Inst[10:0] : 11'bz;  // Controlled_Buffer controlled_buffer_1
  and and_2 (and_2_out, comparator_1_eq, opcode_decoder_1_high_register_op);
  and and_3 (and_3_out, comparator_2_eq, opcode_decoder_1_high_register_op);
  or or_2 (or_2_out, and_3_out, or_13_out, and_4_out);
  assign controlled_buffer_2_out = or_2_out ? Inst[2:0] : 3'bz;  // Controlled_Buffer controlled_buffer_2
  Pull_Resistor pull_resistor_2 (.node(pull_resistor_2_node));
  assign pull_resistor_2_node = and_3_out ? Inst[5:3] : 3'bz;  // Controlled_Buffer controlled_buffer_3
  and and_4 (and_4_out, comparator_3_eq, opcode_decoder_1_high_register_op);
  and and_5 (and_5_out, comparator_4_eq, opcode_decoder_1_high_register_op);
  and and_6 (and_6_out, comparator_5_eq, opcode_decoder_1_high_register_op);
  and and_7 (and_7_out, comparator_6_eq, opcode_decoder_1_high_register_op);
  and and_8 (and_8_out, comparator_7_eq, opcode_decoder_1_high_register_op);
  Conditional conditional_1 (
    .Offset(conditional_1_offset), .Verified(conditional_1_verified), .Instruction(Inst), .Z(Flags[2]),
    .C(Flags[1]), .N(Flags[3]), .V(Flags[0]), .Enable(opcode_decoder_1_conditional));
  Pull_Resistor pull_resistor_3 (.node(controlled_buffer_2_out));
  assign or_3_out = pull_resistor_2_node | pull_resistor_4_node;  // OR_Gate or_3, 3 bits wide
  Pull_Resistor pull_resistor_4 (.node(pull_resistor_4_node));
  assign pull_resistor_4_node = or_13_out ? controlled_buffer_2_out : 3'bz;  // Controlled_Buffer controlled_buffer_4
  Pull_Resistor pull_resistor_5 (.node(pull_resistor_5_node));
  assign pull_resistor_5_node = and_3_out ? 4'b0010 : 4'bz;  // Controlled_Buffer controlled_buffer_5
  Multiplexer #(.select(3), .width(32)) multiplexer_1 (
    .in5(SP), .in6(LR_Value), .in7(and_1_out), .out(multiplexer_1_out), .sel(Inst[5:3]));  // open: in0, in1, in2, in3, in4
  Multiplexer #(.select(3), .width(32)) multiplexer_2 (
    .in0(R0), .in1(R1), .in2(R2), .in3(R3), .in4(R4), .in5(R5), .in6(R6), .in7(R7),
    .out({multiplexer_2_out_2, multiplexer_2_out}), .sel(Inst[5:3]));
  assign bit_extender_1_out = {{24{multiplexer_2_out[7]}}, multiplexer_2_out};  // Bit_Extender bit_extender_1
  assign bit_extender_2_out = {{24{1'b0}}, multiplexer_2_out};  // Bit_Extender bit_extender_2
  Shift_Add_Sub_Mov shift_add_sub_mov_1 (
    .Flags_Update_Mask(shift_add_sub_mov_1_flags_update_mask), .Rm(shift_add_sub_mov_1_rm),
    .Rn(shift_add_sub_mov_1_rn), .Rd(shift_add_sub_mov_1_rd), .Imm5(Imm5), .Imm32(shift_add_sub_mov_1_imm32),
    .ALU_Opcode(shift_add_sub_mov_1_alu_opcode), .Carry(shift_add_sub_mov_1_carry),
    .Imm32_Enable(shift_add_sub_mov_1_imm32_enable), .Instruction(Inst), .Enable(opcode_decoder_1_shift));
  Data_Processing data_processing_1 (
    .Rn(data_processing_1_rn), .Rm(data_processing_1_rm), .ALU_Opcode(data_processing_1_alu_opcode),
    .Flags_Update_Mask(data_processing_1_flags_update_mask), .Rd(data_processing_1_rd), .Instruction(Inst),
    .Enable(opcode_decoder_1_data_processing));
  Flags_APSR flags_apsr_1 (.Update_Mask(or_1_out), .Flags_In(FlagsIn), .Clk(Clk), .Rst(Reset), .Flags_Out(Flags));
  Load_Store load_store_1 (
    .Store(Store), .Load(Load), .PC_Hold(PC_Hold), .RAM_Addr(RAM_Addr), .Mask(Mask),
    .Imm32(load_store_1_imm32), .Rmd(load_store_1_rmd), .Enable(opcode_decoder_1_load_store),
    .Old_Value(RAM_Value), .R5(R5), .R6(R6), .R7(R7), .R0(R0), .R1(R1), .R2(R2), .R3(R3), .R4(R4),
    .Program_Counter(PC), .Instruction(Inst), .Stack_Pointer(SP), .Clk(Clk), .Reset(Reset));
  Load_Address load_address_1 (
    .Enable(opcode_decoder_1_load_address), .Instruction(Inst), .Program_Counter(PC), .Stack_Pointer(SP),
    .Imm32_Enable(load_address_1_imm32_enable), .Rd(load_address_1_rd),
    .ALU_Opcode(load_address_1_alu_opcode), .Imm32(load_address_1_imm32));
  assign bit_extender_3_out = {{21{or_4_out[10]}}, or_4_out};  // Bit_Extender bit_extender_3
  assign or_4_out = conditional_1_offset | pull_resistor_1_node;  // OR_Gate or_4, 11 bits wide
  or or_5 (or_5_out, conditional_1_verified, and_2_out, and_8_out, opcode_decoder_1_long_branch, or_8_out);
  Adder #(.width(32)) adder_2 (.a(PC), .b(32'h2), .out(adder_2_out));  // open: cin, cout
  Register #(.width(32)) Link_Register (.D(adder_2_out), .en(or_6_out), .clk(Clk), .Q(LR_Value));  // open: clr
  or or_6 (or_6_out, opcode_decoder_1_long_branch, and_8_out);
  assign controlled_buffer_6_out = or_7_out ? 4'b1001 : 4'bz;  // Controlled_Buffer controlled_buffer_6
  or or_7 (or_7_out, and_4_out, opcode_decoder_1_signextend);
  Pull_Resistor pull_resistor_6 (.node(pull_resistor_6_node));
  assign pull_resistor_6_node = and_4_out ? negator_1_out : 32'bz;  // Controlled_Buffer controlled_buffer_7
  Negator #(.width(32)) negator_1 (.in(multiplexer_1_out), .out(negator_1_out));
  Pull_Resistor pull_resistor_7 (.node(pull_resistor_7_node));
  assign pull_resistor_7_node = and_5_out ? multiplexer_1_out : 32'bz;  // Controlled_Buffer controlled_buffer_8
  assign controlled_buffer_9_out = and_5_out ? 4'b0101 : 4'bz;  // Controlled_Buffer controlled_buffer_9
  or or_8 (or_8_out, and_6_out, and_7_out);
  Subtractor #(.width(32)) subtractor_1 (
    .a({multiplexer_2_out_2, multiplexer_2_out}), .b(32'h1), .out(subtractor_1_out));  // open: bin, bout
  Adder #(.width(32)) adder_3 (
    .a({multiplexer_2_out_2, multiplexer_2_out}), .b(PC), .out(adder_3_out));  // open: cin, cout
  assign bit_extender_4_out = {{16{multiplexer_2_out_2[15]}}, {multiplexer_2_out_2[15:8], multiplexer_2_out}};  // Bit_Extender bit_extender_4
  assign bit_extender_5_out = {{16{1'b0}}, {multiplexer_2_out_2[15:8], multiplexer_2_out}};  // Bit_Extender bit_extender_5
  SP_Address sp_address_1 (
    .New_Stack_Pointer(sp_address_1_new_stack_pointer), .Write_Enable(sp_address_1_write_enable),
    .Stack_Pointer(SP), .Instruction(Inst), .Enable(opcode_decoder_1_sp_address));
  Adder #(.width(32)) adder_4 (.a(32'h2), .b(bit_extender_3_out), .out(adder_4_out));  // open: cin, cout
  or or_9 (or_9_out, conditional_1_verified, opcode_decoder_1_long_branch);
  Pull_Resistor pull_resistor_8 (.node(controlled_buffer_6_out));
  assign or_10_out = controlled_buffer_6_out | controlled_buffer_9_out;  // OR_Gate or_10, 4 bits wide
  or or_11 (or_11_out, and_4_out, or_13_out);
  assign or_12_out = pull_resistor_6_node | pull_resistor_11_node | pull_resistor_7_node;  // OR_Gate or_12, 32 bits wide
  Pull_Resistor pull_resistor_9 (.node(controlled_buffer_9_out));
  Adder #(.width(32)) adder_5 (.a(adder_3_out), .b(32'h4), .out(adder_5_out));  // open: cin, cout
  Multiplexer #(.width(32)) multiplexer_3 (
    .in0({multiplexer_2_out_2, multiplexer_2_out}), .in1(multiplexer_1_out), .out(multiplexer_3_out),
    .sel(Inst[6]));
  Multiplexer #(.select(2), .width(32)) multiplexer_4 (
    .in0(bit_extender_4_out), .in1(bit_extender_1_out), .in2(bit_extender_5_out), .in3(bit_extender_2_out),
    .out(multiplexer_4_out), .sel(Inst[7:6]));
  Multiplier #(.width(32)) multiplier_1 (.a(32'h2), .b(adder_4_out), .out(multiplier_1_out));  // open: cin, cout
  Adder #(.width(32)) adder_6 (.a(multiplier_1_out), .b(PC), .out(adder_6_out), .cin(1'b0));  // open: cout
  or or_13 (or_13_out, and_5_out, opcode_decoder_1_signextend);
  Multiplexer #(.width(32)) multiplexer_5 (
    .in0(subtractor_1_out), .in1(and_9_out), .out(multiplexer_5_out), .sel(and_7_out));
  assign and_9_out = ~32'h1 & adder_5_out;  // AND_Gate and_9, 32 bits wide
  Pull_Resistor pull_resistor_10 (.node(pull_resistor_10_node));
  assign pull_resistor_10_node = and_8_out ? multiplexer_3_out : 32'bz;  // Controlled_Buffer controlled_buffer_10
  Pull_Resistor pull_resistor_11 (.node(pull_resistor_11_node));
  assign pull_resistor_11_node = opcode_decoder_1_signextend ? negator_2_out : 32'bz;  // Controlled_Buffer controlled_buffer_11
  Negator #(.width(32)) negator_2 (.in(multiplexer_4_out), .out(negator_2_out));
  and and_10 (and_10_out, opcode_decoder_1_shift, ~opcode_decoder_1_data_processing);  // AND_Gate
  not not_1 (not_1_out, PC_Hold);
  assign controlled_buffer_12_out = or_9_out ? adder_6_out : 32'bz;  // Controlled_Buffer controlled_buffer_12
  Pull_Resistor pull_resistor_12 (.node(pull_resistor_12_node));
  assign pull_resistor_12_node = and_2_out ? LR_Value : 32'bz;  // Controlled_Buffer controlled_buffer_13
  assign or_14_out = pull_resistor_13_node | pull_resistor_10_node;  // OR_Gate or_14, 32 bits wide
  Pull_Resistor pull_resistor_13 (.node(pull_resistor_13_node));
  assign pull_resistor_13_node = or_8_out ? multiplexer_5_out : 32'bz;  // Controlled_Buffer controlled_buffer_14
  Multiplexer multiplexer_6 (.in0(Flags[1]), .in1(shift_add_sub_mov_1_carry), .out(Carry), .sel(and_10_out));
  Pull_Resistor pull_resistor_14 (.node(controlled_buffer_12_out));
  not not_2 (not_2_out, or_5_out);
  or or_15 (DP_Shift, and_10_out, opcode_decoder_1_high_register_op);
  or or_16 (Imm32_Enable, shift_add_sub_mov_1_imm32_enable, or_11_out, load_address_1_imm32_enable);
  assign Imm32 = shift_add_sub_mov_1_imm32 | load_store_1_imm32 | load_address_1_imm32 | or_12_out;  // OR_Gate or_17, 32 bits wide
  assign ALU_Opcode = shift_add_sub_mov_1_alu_opcode | data_processing_1_alu_opcode | or_10_out | load_address_1_alu_opcode | pull_resistor_5_node;  // OR_Gate or_18, 4 bits wide
  assign Rm = shift_add_sub_mov_1_rm | data_processing_1_rm | load_store_1_rmd;  // OR_Gate or_19, 3 bits wide
  assign Rn = shift_add_sub_mov_1_rn | data_processing_1_rn | load_store_1_rmd | or_3_out;  // OR_Gate or_20, 3 bits wide
  assign Rd = shift_add_sub_mov_1_rd | data_processing_1_rd | controlled_buffer_2_out | load_store_1_rmd | load_address_1_rd;  // OR_Gate or_21, 3 bits wide
  assign or_22_out = controlled_buffer_12_out | pull_resistor_12_node | or_14_out;  // OR_Gate or_22, 32 bits wide
  Adder #(.width(32)) adder_7 (.a(PC), .b(32'h2), .out(adder_7_out));  // open: cin, cout
  Counter #(.max('hffffffff), .trigger("falling"), .width(32)) counter_1 (
    .clr(Reset), .load(not_1_out), .count(1'b0), .clk(Clk), .D(multiplexer_7_out), .Q(PC));  // open: up, carry
  Multiplexer #(.width(32)) multiplexer_7 (
    .in0(or_22_out), .in1(adder_7_out), .out(multiplexer_7_out), .sel(not_2_out));

  // Other names for the same wires on the sheet: PC_Value[31:0] = PC; SP_Value[31:0] = SP

  // Notes on the sheet:
  //   Extract carry
  //   Extract Opcode
  //   IF Reg_Imm=1 THEN use shift value from register ELSE use shift value from Imm5
  //   Buffer flags for next instruction
  //   Add 3 to offset because ARM pre-increments PC
  //   and does an additional prefetch operation
endmodule
